# Fritzing sketch RPi LCD Verbindung V2 - final (saved by Fritzing 0.9.2b)
stripboards: 1

parts:
  U1 = LCD-16X2 [package=lcd-16x2_noholes]
  S1 = Pushbutton [package="[THT]"]
  LED1 = LED - 5mm [color="Red (633nm)" package="5 mm [THT]"]
  R4 = Trimmer Potentiometer [maximum_resistance=10kΩ package=THT]
  R5 = Resistor [tolerance=±5% resistance=220 package="0805 [SMD]"]
  C1 = Ceramic Capacitor [capacitance=100nF package="100 mil [THT, multilayer]"]
  Raspberry_Pi1 = Raspberry Pi 2
  R3 = Trimmer Potentiometer [maximum_resistance=10kΩ package=THT]
  U2 = Voltage Regulator - 5V [package="TO220 [THT]"]
  J2 = screw terminal, 3 pins
  S2 = Pushbutton [package=THT]

nets:
  GND: U1.VSS, U1.K, R4.leg1, Raspberry_Pi1.GND, R3.leg1, U2.GND, J2.pin3
  N1: U1.VDD, R4.leg2, C1.0, R3.leg2, S2.leg0
  N2: U1.VO, LED1.cathode, R3.wiper
  N3: U1.RS, Raspberry_Pi1.GPIO12
  N4: U1.E, Raspberry_Pi1.GPIO21
  N5: U1.DB5, Raspberry_Pi1.GPIO6
  N6: U1.DB6, Raspberry_Pi1.GPIO17
  N7: U1.DB7, Raspberry_Pi1.GPIO18
  N8: S1.Pin_1, S1.Pin_2, R5.Pin_1, Raspberry_Pi1.GPIO26
  N9: S1.Pin_3, S1.Pin_4, U2.output_voltage
  N10: LED1.anode, R5.Pin_0
  N11: C1.1, U2.input_voltage
  N12: Raspberry_Pi1.5V, J2.pin1, S2.leg1
