# Fritzing sketch RPi LCD Verbindung V3_1 - FAB (saved by Fritzing 0.9.2b)
circuit board: 3.93773cm x 3.25546cm
stripboards: 1

parts:
  S1 = Pushbutton [package="[THT]"]
  LED1 = LED - 5mm [color="Red (633nm)" package="5 mm [THT]"]
  R5 = Resistor [tolerance=±5% resistance=220 package="0805 [SMD]"]
  C1 = Ceramic Capacitor [capacitance=100nF package="100 mil [THT, multilayer]"]
  R3 = Trimmer Potentiometer [maximum_resistance=10kΩ package=THT]
  U2 = Voltage Regulator - 5V [package="TO220 [THT]"]
  S2 = Pushbutton [package=THT]
  J1 = Screw terminal - 2 pins [package=THT]
  J2 = male pin header, 1 pin [form="♂ (male)"]
  J3 = male pin header, 1 pin [form="♂ (male)"]
  J4 = male pin header, 1 pin [form="♂ (male)"]
  J6 = male pin header, 5 pins [form="♂ (male)"]
  J7 = male pin header, 1 pin [form="♂ (male)"]
  R4 = Trimmer Potentiometer [maximum_resistance=10kΩ package=THT]

nets:
  N1: S1.Pin_1, S1.Pin_2, U2.output_voltage
  N2: S1.Pin_3, S1.Pin_4, R5.Pin_1, J2.pin1
  N3: LED1.cathode, R5.Pin_0
  N4: LED1.anode, R3.leg1, U2.input_voltage, J1.pin1, J6.pin1, J6.pin2, J6.pin3, J6.pin4, J6.pin5, R4.leg1
  N5: C1.0, R3.leg2, S2.leg0, J7.pin1, R4.leg2
  N6: C1.1, U2.GND
  N7: R3.wiper, J3.pin1
  N8: S2.leg1, J1.pin2
  N9: J4.pin1, R4.wiper

notes:
  5V
  GND
  3,3V
  backlit
  contrast
  RS   E   D4  D5  D6  D7
  220 Ohm
  LED
  GPIO 12  21  5     6   17  18
