# Fritzing sketch RPi Sensors - V1 (saved by Fritzing 0.9.2b)
stripboards: 1

parts:
  Raspberry_Pi1 = Raspberry Pi 2
  Bauteil1 = Triple Axis Magnetometer - HMC5883 Breakout
  U1 = EM406 GPS Connector [package=em406]
  S1 = Pushbutton [package="[THT]"]
  LED1 = LED - 5mm [color="Red (633nm)" package="5 mm [THT]"]
  R1 = Resistor [tolerance=±5% resistance=220 package="2010 [SMD]"]
  Grove1 = Grove Light Sensor
  Grove2 = Grove Infrared Receiver
  J1 = Screw terminal - 2 pins [package=THT]

nets:
  N1: Raspberry_Pi1.3v3, S1.Pin_1, S1.Pin_2, J1.pin2
  N2: Raspberry_Pi1.GPIO2, Bauteil1.SDA
  N3: Raspberry_Pi1.GPIO3, Bauteil1.SCL
  N4: Raspberry_Pi1.GPIO27, Grove1.SIG
  GND: Raspberry_Pi1.GND, Bauteil1.GND, U1.GND1, LED1.cathode, Grove1.GND, Grove2.GND, J1.pin1
  N5: Raspberry_Pi1.GPIO23, Grove2.RX
  N6: Raspberry_Pi1.GPIO15, U1.TX
  N7: Raspberry_Pi1.GPIO14, U1.GND2
  VCC: Bauteil1.VCC, U1.VCC, S1.Pin_3, S1.Pin_4, R1.Pin_0, Grove1.VCC, Grove2.VCC
  N8: LED1.anode, R1.Pin_1

notes:
  3,3V
  GND
  220Ohm
  3-Axis Compass
  Neo6M GPS
  Light      Sensor
  PIR Infrared
