# Fritzing sketch RPi powerline for sensors - V1 - FAB (saved by Fritzing 0.9.2b)
circuit board: 2.66255cm x 2.73123cm

parts:
  LED1 = LED - 5mm [color="Red (633nm)" package="5 mm [THT]"]
  J1 = Screw terminal - 2 pins [package=THT]
  S1 = Pushbutton [package=THT]
  R2 = Resistor [tolerance=±5% resistance=220 package=THT]
  U1 = Voltage Regulator - 5V [package="TO220 [THT]"]
  C2 = Ceramic Capacitor [capacitance=100nF package="100 mil [THT, multilayer]"]
  J2 = male pin header, 5 pins [form="♂ (male)"]
  U2 = Voltage Regulator - 3.3V [package="TO220 [THT]"]
  J3 = male pin header, 5 pins [form="♂ (male)"]

nets:
  GND: LED1.cathode, J1.pin2, U1.GND, U2.GND
  N1: LED1.anode, R2.Pin_1
  N2: J1.pin1, C2.0
  N3: S1.leg0, R2.Pin_0, J2.pin1, J2.pin2, J2.pin3, J2.pin4, J2.pin5, U2.input_voltage
  N4: S1.leg1, U1.output_voltage
  N5: U1.input_voltage, C2.1
  N6: U2.output_voltage, J3.pin1, J3.pin2, J3.pin3, J3.pin4, J3.pin5

notes:
  5V
  GND
  220 Ohm
  3,3V
