# Fritzing sketch Autonomes Roboter Vehicle (saved by Fritzing 0.9.2b)
breadboards: 1

parts:
  Raspberry_Pi1 = Raspberry Pi 2
  Bauteil1 = Logic Level Converter

nets:
  GND: Raspberry_Pi1.GND, Bauteil1.GND
  N1: Bauteil1.TX2_LV, Bauteil1.TX2_HV
  N2: Bauteil1.RX2_LV, Bauteil1.RX2_HV
  N3: Bauteil1.LV, Bauteil1.HV
  N4: Bauteil1.RX_LV, Bauteil1.RX_HV
  N5: Bauteil1.TX_LV, Bauteil1.TX_HV
