# Fritzing sketch RPi LCD Verbindung V1 (saved by Fritzing 0.9.2b)
stripboards: 1

parts:
  U1 = LCD-16X2 [package=lcd-16x2_noholes]
  S1 = Pushbutton [package="[THT]"]
  LED1 = LED - 5mm [color="Red (633nm)" package="5 mm [THT]"]
  R4 = Trimmer Potentiometer [maximum_resistance=10kΩ package=THT]
  R5 = Resistor [tolerance=±5% resistance=220 package="0805 [SMD]"]
  U2 = Voltage Regulator - 5V [package="TO220 [THT]"]
  C1 = Ceramic Capacitor [capacitance=100nF package="100 mil [THT, multilayer]"]
  Raspberry_Pi1 = Raspberry Pi 2
  R3 = Trimmer Potentiometer [maximum_resistance=10kΩ package=THT]

nets:
  GND: U1.VSS, U1.R_W, U1.K, LED1.cathode, R4.leg1, U2.GND, Raspberry_Pi1.GND, R3.leg1
  VDD: U1.VDD, R4.leg2, C1.0, Raspberry_Pi1.5V, R3.leg2
  N1: U1.VO, R3.wiper
  N2: U1.E, Raspberry_Pi1.GPIO24
  N3: U1.DB4, Raspberry_Pi1.GPIO22
  N4: U1.A, R4.wiper
  N5: S1.Pin_1, S1.Pin_2, R5.Pin_0, Raspberry_Pi1.GPIO21
  N6: S1.Pin_3, S1.Pin_4, U2.output_voltage
  N7: LED1.anode, R5.Pin_1
  N8: U2.input_voltage, C1.1
